// Logisim project 8bit_computer.circ as structural Verilog: 1 circuit, main circuit main
module main (
);

  wire clock_1_out, comparator_1_lt, not_1_out;
  wire [0:0] and_1_out;
  wire [2:1] button_1_out;
  wire [7:0] adder_1_out, adder_2_out, controlled_buffer_1_out, register_1_q, register_2_q, register_3_q,
       register_4_q, register_5_q, register_6_q, register_7_q, rom_1_data;
  wire [27:8] rom_1_data_2;

  Adder adder_1 (.a(rom_1_data), .b({{7{1'b0}}, and_1_out[0]}), .out(adder_1_out));  // open: cin, cout
  Register register_1 (.D(adder_1_out), .Q(register_1_q), .clk(clock_1_out));  // open: en, clr
  Clock clock_1 (.out(clock_1_out));
  and and_1 (and_1_out[0], rom_1_data_2[26], not_1_out);
  Register register_2 (.D(controlled_buffer_1_out), .Q(register_2_q), .clk(rom_1_data_2[25]));  // open: en, clr
  Register register_3 (.D(controlled_buffer_1_out), .Q(register_3_q), .clk(rom_1_data_2[24]));  // open: en, clr
  Comparator #(.mode("unsigned")) comparator_1 (
    .a(register_2_q), .b(register_3_q), .lt(comparator_1_lt));  // open: gt, eq
  ROM #(.dataWidth(28)) rom_1 (.addr(register_1_q), .data({rom_1_data_2, rom_1_data}));  // open: sel
  not not_1 (not_1_out, comparator_1_lt);
  assign controlled_buffer_1_out = rom_1_data_2[16] ? rom_1_data_2[15:8] : 8'bz;  // Controlled_Buffer controlled_buffer_1
  Register register_4 (.D(controlled_buffer_1_out), .Q(register_4_q), .clk(rom_1_data_2[19]));  // open: en, clr
  Register register_5 (.D(controlled_buffer_1_out), .Q(register_5_q), .clk(rom_1_data_2[20]));  // open: en, clr
  Register register_6 (.D(controlled_buffer_1_out), .Q(register_6_q), .clk(rom_1_data_2[22]));  // open: en, clr
  Adder adder_2 (.a(register_4_q), .b(register_5_q), .out(adder_2_out));  // open: cin, cout
  assign controlled_buffer_1_out = rom_1_data_2[18] ? adder_2_out : 8'bz;  // Controlled_Buffer controlled_buffer_2
  RAM ram_1 (
    .addr(register_6_q), .data(controlled_buffer_1_out), .clk(rom_1_data_2[23]), .ld(rom_1_data_2[21]));  // open: sel, clr
  Hex_Digit_Display hex_digit_display_1 (.value(register_7_q[7:4]));  // open: dp
  Register register_7 (.D(controlled_buffer_1_out), .Q(register_7_q), .clk(rom_1_data_2[17]));  // open: en, clr
  Button button_1 (.out(button_1_out[1]));
  Button button_2 (.out(button_1_out[2]));
  assign controlled_buffer_1_out = rom_1_data_2[27] ? {{5{1'b0}}, button_1_out, 1'b0} : 8'bz;  // Controlled_Buffer controlled_buffer_3
  Hex_Digit_Display hex_digit_display_2 (.value(register_7_q[3:0]));  // open: dp
endmodule
