// Logisim project 1-1 基础原件.circ as structural Verilog: 1 circuit, main circuit main
module main (
);

  wire clock_1_out, clock_2_out, clock_3_out, clock_4_out, clock_5_out, clock_6_out;
  wire [3:0] clock_10_out;

  LED led_1 (.in(clock_1_out));
  Clock clock_1 (.out(clock_1_out));
  LED led_2 (.in(clock_3_out));
  LED led_3 (.in(clock_2_out));
  Clock clock_2 (.out(clock_2_out));
  Clock clock_3 (.out(clock_3_out));
  LED led_4 (.in(clock_4_out));
  LED led_5 (.in(clock_4_out));
  Clock clock_4 (.out(clock_4_out));
  LED led_6 (.in(clock_5_out));
  LED led_7 (.in(clock_6_out));
  Clock clock_5 (.out(clock_5_out));
  Clock clock_6 (.out(clock_6_out));
  LED led_8 (.in(1'b1));
  LED led_9 (.in(clock_10_out[3]));
  Clock clock_7 (.out(clock_10_out[3]));
  LED led_10 (.in(1'b0));
  LED led_11 (.in(clock_10_out[2]));
  LED led_12 (.in(clock_10_out[1]));
  Clock clock_8 (.out(clock_10_out[2]));
  Clock clock_9 (.out(clock_10_out[1]));
  LED led_13 (.in(clock_10_out[0]));
  Clock clock_10 (.out(clock_10_out[0]));
endmodule
