// Logisim project 1-2 二进制数字演示.circ as structural Verilog: 1 circuit, main circuit main
module main (
);

  LED led_1 (.in(1'b0));
  LED led_2 (.in(1'b0));
  LED led_3 (.in(1'b1));
  LED led_4 (.in(1'b1));
  Hex_Digit_Display hex_digit_display_1 (.value(4'b0101));  // open: dp
  LED led_5 (.in(1'b0));
  LED led_6 (.in(1'b1));
  LED led_7 (.in(1'b0));
  LED led_8 (.in(1'b1));
  Hex_Digit_Display hex_digit_display_2 (.value(4'b0101));  // open: dp
endmodule
