// Logisim project 2-1 逻辑门演示.circ as structural Verilog: 1 circuit, main circuit main
module main (
);

  wire and_1_out, and_2_out, and_3_out, and_4_out, clock_1_out, clock_2_out, clock_3_out, clock_4_out,
       clock_5_out, clock_6_out, clock_7_out, clock_8_out, clock_9_out, clock_10_out, clock_11_out,
       clock_12_out, clock_13_out, clock_14_out, clock_15_out, clock_16_out, clock_17_out, clock_18_out,
       clock_19_out, not_1_out, not_2_out, not_3_out, not_4_out, or_1_out, or_2_out, or_3_out, or_4_out,
       or_5_out;

  Clock clock_1 (.out(clock_1_out));
  Clock clock_2 (.out(clock_2_out));
  Clock clock_3 (.out(clock_3_out));
  Clock clock_4 (.out(clock_4_out));
  Clock clock_5 (.out(clock_5_out));
  Clock clock_6 (.out(clock_6_out));
  Clock clock_7 (.out(clock_7_out));
  Clock clock_8 (.out(clock_8_out));
  Clock clock_9 (.out(clock_9_out));
  Clock clock_10 (.out(clock_10_out));
  Clock clock_11 (.out(clock_11_out));
  not not_1 (not_1_out, clock_1_out);
  LED led_1 (.in(not_1_out));
  or or_1 (or_1_out, clock_2_out, clock_3_out);
  LED led_2 (.in(or_1_out));
  LED led_3 (.in(and_1_out));
  and and_1 (and_1_out, clock_4_out, clock_5_out);
  or or_2 (or_2_out, clock_6_out, clock_7_out, clock_8_out);
  LED led_4 (.in(or_2_out));
  and and_2 (and_2_out, clock_9_out, clock_10_out, clock_11_out);
  LED led_5 (.in(and_2_out));
  Clock clock_12 (.out(clock_12_out));
  Clock clock_13 (.out(clock_13_out));
  Clock clock_14 (.out(clock_14_out));
  Clock clock_15 (.out(clock_15_out));
  Clock clock_16 (.out(clock_16_out));
  Clock clock_17 (.out(clock_17_out));
  Clock clock_18 (.out(clock_18_out));
  Clock clock_19 (.out(clock_19_out));
  not not_2 (not_2_out, clock_12_out);
  not not_3 (not_3_out, clock_13_out);
  or or_3 (or_3_out, clock_15_out, clock_16_out);
  and and_3 (and_3_out, clock_18_out, clock_19_out);
  not not_4 (not_4_out, or_4_out);
  or or_4 (or_4_out, not_2_out, not_3_out);
  or or_5 (or_5_out, clock_14_out, or_3_out);
  and and_4 (and_4_out, clock_17_out, and_3_out);
  LED led_6 (.in(not_4_out));
  LED led_7 (.in(or_5_out));
  LED led_8 (.in(and_4_out));

  // Notes on the sheet:
  //   非门
  //   或门
  //   与门
  //   多输入或门
  //   多输入与门
  //   等同于
  //   等同于
  //   等同于
endmodule
