// Logisim project 3-1 锁存器演示.circ as structural Verilog: 1 circuit, main circuit main
module main (
);

  wire and_1_out, and_2_out, clock_1_out, clock_2_out, clock_3_out, clock_4_out, clock_5_out, d_ff_1_q,
       not_1_out, or_1_out, or_2_out, or_3_out;

  Clock clock_1 (.out(clock_1_out));
  Clock clock_2 (.out(clock_2_out));
  Clock clock_3 (.out(clock_3_out));
  and and_1 (and_1_out, or_1_out, clock_1_out);
  not not_1 (not_1_out, clock_1_out);
  LED led_1 (.in(or_1_out));
  or or_1 (or_1_out, and_1_out, and_2_out);
  and and_2 (and_2_out, not_1_out, clock_4_out);
  Clock clock_4 (.out(clock_4_out));
  D_Flip_Flop #(.trigger("low")) d_ff_1 (
    .clk(clock_2_out), .D(clock_3_out), .Q(d_ff_1_q));  // open: Qn, preset, en, reset
  LED led_2 (.in(d_ff_1_q));
  LED led_3 (.in(or_2_out));
  or or_2 (or_2_out, 1'b0, clock_5_out);
  Clock clock_5 (.out(clock_5_out));
  LED led_4 (.in(or_3_out));
  or or_3 (or_3_out, or_3_out, 1'b0);

  // Notes on the sheet:
  //   锁存信号
  //   锁存信号
  //   输入信号
  //   与门
  //   非门
  //   发光二极管
  //   或门
  //   与门
  //   输入信号
  //   当锁存信号为0的时候
  //   发光二极管
  //   或门
  //   输入信号
  //   发光二极管
  //   或门
  //   当锁存信号为1的时候
endmodule
