// Logisim project 3-2 触发器演示.circ as structural Verilog: 1 circuit, main circuit main
module main (
);

  wire clock_1_out, clock_2_out, clock_3_out, clock_4_out, d_ff_1_q, d_ff_2_q, d_ff_3_q, not_1_out, not_2_out;

  not not_1 (not_1_out, clock_1_out);
  Clock clock_1 (.out(clock_1_out));
  Clock clock_2 (.out(clock_2_out));
  not not_2 (not_2_out, not_1_out);
  D_Flip_Flop #(.trigger("low")) d_ff_1 (
    .clk(not_2_out), .D(clock_2_out), .Q(d_ff_1_q));  // open: Qn, preset, en, reset
  LED led_1 (.in(d_ff_2_q));
  D_Flip_Flop #(.trigger("low")) d_ff_2 (.clk(not_1_out), .D(d_ff_1_q), .Q(d_ff_2_q));  // open: Qn, preset, en, reset
  Clock clock_3 (.out(clock_3_out));
  Clock clock_4 (.out(clock_4_out));
  D_Flip_Flop d_ff_3 (.clk(clock_3_out), .D(clock_4_out), .Q(d_ff_3_q));  // open: Qn, preset, en, reset
  LED led_2 (.in(d_ff_3_q));

  // Notes on the sheet:
  //   触发信号
  //   非门
  //   输入信号
  //   非门
  //   锁存器
  //   发光二极管
  //   锁存器
  //   等同于
  //   触发信号
  //   输入信号
  //   发光二极管
  //   触发器
endmodule
