// Logisim project 4-2 Rom只读存储器.circ as structural Verilog: 1 circuit, main circuit main
module main (
);

  wire and_1_out, and_2_out, and_3_out, and_4_out, clock_1_out, clock_2_out, not_1_out, not_2_out, not_3_out,
       not_4_out;
  wire [1:0] clock_4_out;
  wire [3:0] and_17_out, and_18_out, and_19_out, and_20_out, or_1_out, rom_1_data;

  Clock clock_1 (.out(clock_1_out));
  Clock clock_2 (.out(clock_2_out));
  not not_1 (not_1_out, clock_1_out);
  not not_2 (not_2_out, clock_2_out);
  not not_3 (not_3_out, clock_1_out);
  not not_4 (not_4_out, clock_2_out);
  and and_1 (and_1_out, not_1_out, not_2_out);
  and and_2 (and_2_out, not_3_out, clock_2_out);
  and and_3 (and_3_out, clock_1_out, not_4_out);
  and and_4 (and_4_out, clock_1_out, clock_2_out);
  and and_5 (and_17_out[3], and_1_out, 1'b1);
  and and_6 (and_17_out[2], and_1_out, 1'b0);
  and and_7 (and_18_out[3], and_2_out, 1'b0);
  and and_8 (and_18_out[2], and_2_out, 1'b0);
  and and_9 (and_19_out[2], and_3_out, 1'b0);
  and and_10 (and_19_out[3], and_3_out, 1'b1);
  and and_11 (and_20_out[3], and_4_out, 1'b0);
  and and_12 (and_20_out[2], and_4_out, 1'b0);
  and and_13 (and_17_out[1], and_1_out, 1'b0);
  and and_14 (and_18_out[1], and_2_out, 1'b0);
  and and_15 (and_19_out[1], and_3_out, 1'b0);
  and and_16 (and_20_out[1], and_4_out, 1'b1);
  and and_17 (and_17_out[0], and_1_out, 1'b0);
  and and_18 (and_18_out[0], and_2_out, 1'b0);
  and and_19 (and_19_out[0], and_3_out, 1'b1);
  and and_20 (and_20_out[0], and_4_out, 1'b0);
  assign or_1_out = and_17_out | and_18_out | and_19_out | and_20_out;  // OR_Gate or_1, 4 bits wide
  Hex_Digit_Display hex_digit_display_1 (.value(or_1_out));  // open: dp
  Clock clock_3 (.out(clock_4_out[1]));
  Clock clock_4 (.out(clock_4_out[0]));
  Hex_Digit_Display hex_digit_display_2 (.value(rom_1_data));  // open: dp
  ROM #(.addrWidth(2), .dataWidth(4)) rom_1 (.addr(clock_4_out), .data(rom_1_data));  // open: sel

  // Notes on the sheet:
  //   4个4bit的ROM
  //   等同于
  //   内置ROM
  //   contents of rom_1 (hex, n*v repeats v):
  //   8 0 9 2
endmodule
