// Logisim project 4-3 数码管.circ as structural Verilog: 1 circuit, main circuit main
module main (
);

  wire [3:0] clock_4_out, clock_8_out;
  wire [6:0] rom_1_data;

  Clock clock_1 (.out(clock_4_out[3]));
  Hex_Digit_Display hex_digit_display_1 (.value(clock_4_out));  // open: dp
  Clock clock_2 (.out(clock_4_out[1]));
  Clock clock_3 (.out(clock_4_out[2]));
  Clock clock_4 (.out(clock_4_out[0]));
  Clock clock_5 (.out(clock_8_out[3]));
  Clock clock_6 (.out(clock_8_out[1]));
  Clock clock_7 (.out(clock_8_out[2]));
  Clock clock_8 (.out(clock_8_out[0]));
  ROM #(.addrWidth(4), .dataWidth(7)) rom_1 (.addr(clock_8_out), .data(rom_1_data));  // open: sel
  LED led_1 (.in(rom_1_data[5]));
  LED led_2 (.in(rom_1_data[5]));
  LED led_3 (.in(rom_1_data[5]));
  LED led_4 (.in(rom_1_data[4]));
  LED led_5 (.in(rom_1_data[4]));
  LED led_6 (.in(rom_1_data[4]));
  LED led_7 (.in(rom_1_data[0]));
  LED led_8 (.in(rom_1_data[0]));
  LED led_9 (.in(rom_1_data[0]));
  LED led_10 (.in(rom_1_data[1]));
  LED led_11 (.in(rom_1_data[1]));
  LED led_12 (.in(rom_1_data[1]));
  LED led_13 (.in(rom_1_data[6]));
  LED led_14 (.in(rom_1_data[6]));
  LED led_15 (.in(rom_1_data[6]));
  LED led_16 (.in(rom_1_data[2]));
  LED led_17 (.in(rom_1_data[2]));
  LED led_18 (.in(rom_1_data[2]));
  LED led_19 (.in(rom_1_data[3]));
  LED led_20 (.in(rom_1_data[3]));
  LED led_21 (.in(rom_1_data[3]));

  // Notes on the sheet:
  //   等同于
  //   contents of rom_1 (hex, n*v repeats v):
  //   3f 6 5b 4f 66 6d 7d 7 7f 6f 77 7c 39 5e 79 71
endmodule
