// Logisim project 4-4 Ram读写存储器.circ as structural Verilog: 1 circuit, main circuit main
module main (
);

  wire and_1_out, and_2_out, and_3_out, and_4_out, and_5_out, and_6_out, and_7_out, and_8_out, clock_1_out,
       clock_2_out, clock_3_out, clock_4_out, clock_5_out, clock_6_out, decoder_1_out0, decoder_1_out1,
       decoder_1_out2, decoder_1_out3;
  wire [1:0] controlled_buffer_1_out, ram_1_data, register_1_q, register_2_q, register_3_q, register_4_q,
       register_5_q, register_6_q;

  Clock clock_1 (.out(clock_1_out));
  Clock clock_2 (.out(clock_2_out));
  Clock clock_3 (.out(clock_3_out));
  Clock clock_4 (.out(clock_4_out));
  Clock clock_5 (.out(clock_5_out));
  Clock clock_6 (.out(clock_6_out));
  Register #(.width(2)) register_1 (.D(2'b10), .Q(register_1_q), .clk(clock_4_out));  // open: en, clr
  Register #(.width(2)) register_2 (.D(2'b10), .Q(register_2_q), .clk(clock_1_out));  // open: en, clr
  Decoder #(.select(2)) decoder_1 (
    .out0(decoder_1_out0), .out1(decoder_1_out1), .out2(decoder_1_out2), .out3(decoder_1_out3),
    .sel(register_2_q));  // open: en
  RAM #(.addrWidth(2), .dataWidth(2)) ram_1 (
    .addr(register_1_q), .data(ram_1_data), .clk(clock_5_out), .ld(clock_6_out));  // open: sel, clr
  and and_1 (and_1_out, decoder_1_out0, clock_2_out);
  and and_2 (and_2_out, decoder_1_out1, clock_2_out);
  and and_3 (and_3_out, decoder_1_out2, clock_2_out);
  and and_4 (and_4_out, decoder_1_out3, clock_2_out);
  Hex_Digit_Display hex_digit_display_1 (.value({2'b00, ram_1_data}));  // open: dp
  Register #(.width(2)) register_3 (.D(2'b11), .Q(register_3_q), .clk(and_1_out));  // open: en, clr
  Register #(.width(2)) register_4 (.D(2'b11), .Q(register_4_q), .clk(and_2_out));  // open: en, clr
  Register #(.width(2)) register_5 (.D(2'b11), .Q(register_5_q), .clk(and_3_out));  // open: en, clr
  Register #(.width(2)) register_6 (.D(2'b11), .Q(register_6_q), .clk(and_4_out));  // open: en, clr
  and and_5 (and_5_out, decoder_1_out0, clock_3_out);
  and and_6 (and_6_out, decoder_1_out1, clock_3_out);
  and and_7 (and_7_out, decoder_1_out2, clock_3_out);
  and and_8 (and_8_out, decoder_1_out3, clock_3_out);
  assign controlled_buffer_1_out = and_5_out ? register_3_q : 2'bz;  // Controlled_Buffer controlled_buffer_1
  assign controlled_buffer_1_out = and_6_out ? register_4_q : 2'bz;  // Controlled_Buffer controlled_buffer_2
  assign controlled_buffer_1_out = and_7_out ? register_5_q : 2'bz;  // Controlled_Buffer controlled_buffer_3
  assign controlled_buffer_1_out = and_8_out ? register_6_q : 2'bz;  // Controlled_Buffer controlled_buffer_4
  Hex_Digit_Display hex_digit_display_2 (.value({2'b00, controlled_buffer_1_out}));  // open: dp
  // also tied to VCC on the sheet: {ram_1_data[0], ram_1_data[1]}

  // Notes on the sheet:
  //   数据输入
  //   地址输入
  //   地址控制
  //   数据控制
  //   输出控制
  //   数据输入
  //   地址输入
  //   地址控制
  //   数据控制
  //   输出控制
  //   几乎等同于如下内置内存元件，除了共用输入输出端外
endmodule
