// Logisim project 4-5 加法器演示 .circ as structural Verilog: 1 circuit, main circuit main
module main (
);

  wire [0:0] rom_2_data, rom_3_data, rom_4_data;
  wire [1:0] rom_5_data;
  wire [2:0] clock_1_out, clock_2_out, clock_4_out;
  wire [2:1] clock_3_out;
  wire [3:0] adder_1_out, rom_1_data;

  Adder #(.width(4)) adder_1 (.a(4'b0001), .b(4'b0011), .out(adder_1_out));  // open: cin, cout
  ROM #(.dataWidth(4)) rom_1 (.addr(8'h31), .data(rom_1_data));  // open: sel
  Hex_Digit_Display hex_digit_display_1 (.value(rom_1_data));  // open: dp
  Hex_Digit_Display hex_digit_display_2 (.value(adder_1_out));  // open: dp
  Clock clock_1 (.out(clock_1_out[1]));
  Clock clock_2 (.out(clock_2_out[1]));
  Clock clock_3 (.out(clock_3_out[1]));
  Clock clock_4 (.out(clock_4_out[1]));
  Clock clock_5 (.out(clock_4_out[2]));
  Clock clock_6 (.out(clock_1_out[2]));
  Clock clock_7 (.out(clock_3_out[2]));
  Clock clock_8 (.out(clock_2_out[2]));
  ROM #(.addrWidth(3), .dataWidth(2)) rom_2 (
    .addr({clock_3_out, 1'b0}), .data({clock_2_out[0], rom_2_data[0]}));  // open: sel
  ROM #(.addrWidth(3), .dataWidth(2)) rom_3 (.addr(clock_2_out), .data({clock_4_out[0], rom_3_data[0]}));  // open: sel
  ROM #(.addrWidth(3), .dataWidth(2)) rom_4 (.addr(clock_4_out), .data({clock_1_out[0], rom_4_data[0]}));  // open: sel
  ROM #(.addrWidth(3), .dataWidth(2)) rom_5 (.addr(clock_1_out), .data(rom_5_data));  // open: sel
  Hex_Digit_Display hex_digit_display_3 (.value({rom_5_data[0], rom_4_data[0], rom_3_data[0], rom_2_data[0]}));  // open: dp

  // Notes on the sheet:
  //   使用ROM配表制作的加法器，上下作为对比
  //   contents of rom_1 (hex, n*v repeats v):
  //   0 1 2 3 4 5 6 7 8 9 a b c d e f 1 2 3 4 5 6 7 8 9 a b c d e f 0 2 3 4 5 6 7 8 9 a b c d e f 0 1 3 4
  //   5 6 7 8 9 a b c d e f 0 1 2 4 5 6 7 8 9 a b c d e f 0 1 2 3 5 6 7 8 9 a b c d e f 0 1 2 3 4 6 7 8 9
  //   a b c d e f 0 1 2 3 4 5 7 8 9 a b c d e f 0 1 2 3 4 5 6 8 9 a b c d e f 0 1 2 3 4 5 6 7 9 a b c d e
  //   f 0 1 2 3 4 5 6 7 8 a b c d e f 0 1 2 3 4 5 6 7 8 9 b c d e f 0 1 2 3 4 5 6 7 8 9 a c d e f 0 1 2 3
  //   4 5 6 7 8 9 a b d e f 0 1 2 3 4 5 6 7 8 9 a b c e f 0 1 2 3 4 5 6 7 8 9 a b c d f 0 1 2 3 4 5 6 7 8
  //   9 a b c d e
  //   扩展内容：使用ROM制作带进位的加法器，可以节省大量内存
  //   原理简介：和10进制的加法进位原理一模一样
  //   有3个输入端，原来2个输入端作用不变，额外增加一个进位
  //   把进位结果和它们一起进行加法求和计算
  //   contents of rom_2 (hex, n*v repeats v):
  //   0 1 1 2 1 2 2 3
  //   contents of rom_3 (hex, n*v repeats v):
  //   0 1 1 2 1 2 2 3
  //   contents of rom_4 (hex, n*v repeats v):
  //   0 1 1 2 1 2 2 3
  //   contents of rom_5 (hex, n*v repeats v):
  //   0 1 1 2 1 2 2 3
endmodule
