// Logisim project 4-6 比较器演示 .circ as structural Verilog: 1 circuit, main circuit main
module main (
);

  wire adder_1_cout, adder_2_cout, comparator_1_lt, not_1_out, or_1_out, rom_1_data;
  wire [3:0] adder_1_out, clock_1_out, clock_5_out, not_2_out;

  Comparator #(.width(4)) comparator_1 (.a(4'b0001), .b(4'b0011), .lt(comparator_1_lt));  // open: gt, eq
  ROM #(.dataWidth(1)) rom_1 (.addr(8'h13), .data(rom_1_data));  // open: sel
  not not_1 (not_1_out, comparator_1_lt);
  LED led_1 (.in(rom_1_data));
  LED led_2 (.in(not_1_out));
  Clock clock_1 (.out(clock_1_out[0]));
  Clock clock_2 (.out(clock_1_out[1]));
  Clock clock_3 (.out(clock_1_out[2]));
  Clock clock_4 (.out(clock_1_out[3]));
  Clock clock_5 (.out(clock_5_out[0]));
  Clock clock_6 (.out(clock_5_out[1]));
  Clock clock_7 (.out(clock_5_out[2]));
  Clock clock_8 (.out(clock_5_out[3]));
  assign not_2_out = ~clock_5_out;  // NOT_Gate not_2, 4 bits wide
  Adder #(.width(4)) adder_1 (.a(not_2_out), .b(4'b0001), .out(adder_1_out), .cout(adder_1_cout));  // open: cin
  Adder #(.width(4)) adder_2 (.a(clock_1_out), .b(adder_1_out), .cout(adder_2_cout));  // open: out, cin
  or or_1 (or_1_out, adder_2_cout, adder_1_cout);
  LED led_3 (.in(or_1_out));

  // Notes on the sheet:
  //   使用ROM制作的比较器，上下作为对比
  //   contents of rom_1 (hex, n*v repeats v):
  //   1 15*0 1 1 14*0 1 1 1 13*0 4*1 12*0 5*1 11*0 6*1 10*0 7*1 9*0 8*1 8*0 9*1 7*0 10*1 6*0 11*1 5*0 12*1
  //   4*0 13*1 0 0 0 14*1 0 0 15*1 0 16*1
  //   原理简介：
  //   扩展内容：使用加法器制作的比较器，这样可以节省大量内存
  //   即我们可以通过溢出位来判断A和B的大小
  //   设输入端为A和B，4位二进制数字如果数到16就会进位溢出
  //   考虑公式A+16-B，当A<B的时候，不会溢出，当A>=B的时候，会溢出
  //   其中，16-B等同于把B的每一位取反再加1。最后再与A相加
  //   结果只要有加法溢位，就说明A>=B。所以把它们溢出位进行一下“或”计算
endmodule
