// Logisim project computer3.circ as structural Verilog: 1 circuit, main circuit main
module main (
);

  wire clock_1_out;
  wire [3:0] adder_1_out, controlled_buffer_1_out, register_1_q, register_2_q, register_3_q, register_4_q,
       register_5_q;
  wire [15:0] rom_1_data;

  Register #(.width(4)) register_1 (.D(rom_1_data[3:0]), .Q(register_1_q), .clk(clock_1_out));  // open: en, clr
  Clock clock_1 (.out(clock_1_out));
  ROM #(.addrWidth(4), .dataWidth(16)) rom_1 (.addr(register_1_q), .data(rom_1_data));  // open: sel
  assign controlled_buffer_1_out = rom_1_data[8] ? rom_1_data[7:4] : 4'bz;  // Controlled_Buffer controlled_buffer_1
  Register #(.width(4)) register_2 (
    .D(controlled_buffer_1_out), .Q(register_2_q), .clk(rom_1_data[14]));  // open: en, clr
  Register #(.width(4)) register_3 (
    .D(controlled_buffer_1_out), .Q(register_3_q), .clk(rom_1_data[11]));  // open: en, clr
  Register #(.width(4)) register_4 (
    .D(controlled_buffer_1_out), .Q(register_4_q), .clk(rom_1_data[12]));  // open: en, clr
  Adder #(.width(4)) adder_1 (.a(register_3_q), .b(register_4_q), .out(adder_1_out));  // open: cin, cout
  assign controlled_buffer_1_out = rom_1_data[10] ? adder_1_out : 4'bz;  // Controlled_Buffer controlled_buffer_2
  RAM #(.addrWidth(4), .dataWidth(4)) ram_1 (
    .addr(register_2_q), .data(controlled_buffer_1_out), .clk(rom_1_data[15]), .ld(rom_1_data[13]));  // open: sel, clr
  Hex_Digit_Display hex_digit_display_1 (.value(register_5_q));  // open: dp
  Register #(.width(4)) register_5 (
    .D(controlled_buffer_1_out), .Q(register_5_q), .clk(rom_1_data[9]));  // open: en, clr

  // Notes on the sheet:
  //   contents of rom_1 (hex, n*v repeats v):
  //   121 922 133 1134 175 4176 407 8408 2009 2209
endmodule
