// Logisim project computer5.circ as structural Verilog: 1 circuit, main circuit main
module main (
);

  wire clock_1_out, comparator_1_lt, not_1_out;
  wire [0:0] and_1_out;
  wire [2:1] button_2_out;
  wire [3:0] adder_1_out, adder_2_out, controlled_buffer_1_out, register_1_q, register_2_q, register_3_q,
       register_4_q, register_5_q, register_6_q, register_7_q, rom_1_data;
  wire [19:4] rom_1_data_2;

  Adder #(.width(4)) adder_1 (.a(rom_1_data), .b({3'b000, and_1_out[0]}), .out(adder_1_out));  // open: cin, cout
  Register #(.width(4)) register_1 (.D(adder_1_out), .Q(register_1_q), .clk(clock_1_out));  // open: en, clr
  Clock clock_1 (.out(clock_1_out));
  and and_1 (and_1_out[0], rom_1_data_2[18], not_1_out);
  Register #(.width(4)) register_2 (
    .D(controlled_buffer_1_out), .Q(register_2_q), .clk(rom_1_data_2[17]));  // open: en, clr
  Register #(.width(4)) register_3 (
    .D(controlled_buffer_1_out), .Q(register_3_q), .clk(rom_1_data_2[16]));  // open: en, clr
  Comparator #(.width(4), .mode("unsigned")) comparator_1 (
    .a(register_2_q), .b(register_3_q), .lt(comparator_1_lt));  // open: gt, eq
  ROM #(.addrWidth(4), .dataWidth(20)) rom_1 (.addr(register_1_q), .data({rom_1_data_2, rom_1_data}));  // open: sel
  not not_1 (not_1_out, comparator_1_lt);
  assign controlled_buffer_1_out = rom_1_data_2[8] ? rom_1_data_2[7:4] : 4'bz;  // Controlled_Buffer controlled_buffer_1
  Register #(.width(4)) register_4 (
    .D(controlled_buffer_1_out), .Q(register_4_q), .clk(rom_1_data_2[11]));  // open: en, clr
  Register #(.width(4)) register_5 (
    .D(controlled_buffer_1_out), .Q(register_5_q), .clk(rom_1_data_2[12]));  // open: en, clr
  Register #(.width(4)) register_6 (
    .D(controlled_buffer_1_out), .Q(register_6_q), .clk(rom_1_data_2[14]));  // open: en, clr
  assign controlled_buffer_1_out = rom_1_data_2[10] ? adder_2_out : 4'bz;  // Controlled_Buffer controlled_buffer_2
  Adder #(.width(4)) adder_2 (.a(register_4_q), .b(register_5_q), .out(adder_2_out));  // open: cin, cout
  RAM #(.addrWidth(4), .dataWidth(4)) ram_1 (
    .addr(register_6_q), .data(controlled_buffer_1_out), .clk(rom_1_data_2[15]), .ld(rom_1_data_2[13]));  // open: sel, clr
  Hex_Digit_Display hex_digit_display_1 (.value(register_7_q));  // open: dp
  Register #(.width(4)) register_7 (
    .D(controlled_buffer_1_out), .Q(register_7_q), .clk(rom_1_data_2[9]));  // open: en, clr
  Button button_1 (.out(button_2_out[2]));
  Button button_2 (.out(button_2_out[1]));
  assign controlled_buffer_1_out = rom_1_data_2[19] ? {1'b0, button_2_out, 1'b0} : 4'bz;  // Controlled_Buffer controlled_buffer_3

  // Notes on the sheet:
  //   contents of rom_1 (hex, n*v repeats v):
  //   80001 80202
endmodule
